# Fritzing sketch Layout_Breadboard (saved by Fritzing 0.9.10b)
circuit board: 8.46667cm x 5.64444cm
breadboards: 1

parts:
  SD-Card_Holder = Adafruit SDIO microSD Breakout
  GPS_Modul = Adafruit Ultimate GPS v3 [part_number="Adafruit #746"]
  RP2040_Connect = Arduino Nano RP2040
  Power_IN = Screw terminal - 2 pins [package=THT]

nets:
  3.3V: SD-Card_Holder.3.3V, GPS_Modul.VIN, RP2040_Connect.3V3
  GND: SD-Card_Holder.GND, GPS_Modul.GND, RP2040_Connect.GND, Power_IN.pin2
  N1: SD-Card_Holder.SCLK, RP2040_Connect.D13~
  N2: SD-Card_Holder.DO, RP2040_Connect.D12~/MISO
  N3: SD-Card_Holder.DI, RP2040_Connect.D11/MOSI
  N4: SD-Card_Holder.CS, RP2040_Connect.D10~
  N5: GPS_Modul.RX, RP2040_Connect.TX
  N6: GPS_Modul.TX, RP2040_Connect.RX
  N7: RP2040_Connect.VIN, Power_IN.pin1

notes:
  MotoData V 0-1
  +
  -

custom parts:
  Adafruit Ultimate GPS v3: We carry a few different GPS modules here in the Adafruit shop, but none that satisfied our every desire - that's why we designed this little GPS breakout board. We believe this is the Ultimate GPS module, so we named it that. It's got everything you want and more: -165 dBm sensitivity, 10 Hz updates, 66 channels 5V friendly design and only 20mA current draw Breadboard friendly + two mounting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
  Arduino Nano RP2040: At the core of the Arduino Nano RP2040 Connect is the Raspberry Pi RP2040; a dual-core Arm Cortex M0+ processor, with the on-board ESP32 being available as a co-processor. There’s 16MB of flash memory that’s off-chip, providing plenty of room for code and storage. The highly adaptable u-blox NINA-W102 WiFi and Bluetooth radio module provides connectivity, allowing the device to harness the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
