# Fritzing sketch Layout_Breadboard (saved by Fritzing 0.9.10b)
breadboards: 1

parts:
  M5Stack_Core_(Back)1 = M5Stack Core (Back)
  AM1 = AM2320 Humidity and Temperature Sensor [part_number="Adafruit #3721"]
  Bauteil1 = Voltage Sensor 25V

nets:
  3V3: M5Stack_Core_(Back)1.3V3, AM1.VDD
  N1: M5Stack_Core_(Back)1.Gnd#2, AM1.GND
  N2: M5Stack_Core_(Back)1.21, AM1.SDA
  N3: M5Stack_Core_(Back)1.22, AM1.SCL
  N4: M5Stack_Core_(Back)1.Gnd#31, Bauteil1.-
  5V: M5Stack_Core_(Back)1.5V, Bauteil1.VCC, Bauteil1.+
  N5: M5Stack_Core_(Back)1.35, Bauteil1.S

custom parts:
  M5Stack Core (Back): M5Stack ESP32 development kit
  AM2320 Humidity and Temperature Sensor: AM2320 I2C Humidity and Temperature Sensor
